# Fritzing sketch Master (saved by Fritzing 0.9.3b)
breadboards: 1

parts:
  S4 = Toggle Switch [package=THT]
  R5 = Resistor [tolerance=±5% resistance=100 package=THT]
  C1 = Capacitor Polarized [package=panasonic_c]
  Part4 = Bluetooth HC-05 Macho
  VCC1 = Battery block 9V
  GY1 = MPU-6050 Board GY-521 [form="♀ (female)" package=THT]
  Part5 = Arduino Uno (Rev3)

nets:
  N1: S4.L1, VCC1.+
  VCC: S4.COM, C1.+, Part4.VCC, GY1.pin1, Part5.VIN
  N2: S4.L2, R5.Pin_0
  GND: R5.Pin_1, C1.-, Part4.GND, VCC1.-, GY1.pin2, Part5.GND
  N3: GY1.pin3, Part5.A5/SCL
  N4: GY1.pin4, Part5.A4/SDA
  N5: GY1.pin8, Part5.D2

custom parts:
  MPU-6050 Board GY-521: Acelerometro y Giroscopio MPU-6050 Board GY-521
