# Fritzing sketch Slave (saved by Fritzing 0.9.3b)
breadboards: 1

parts:
  S4 = Toggle Switch [package=THT]
  R5 = Resistor [tolerance=±5% resistance=100 package=THT]
  C1 = Capacitor Polarized [package=panasonic_c]
  Part4 = Bluetooth HC-05 Macho
  R6 = Resistor [tolerance=±5% resistance=100 package=THT]
  R7 = Resistor [tolerance=±5% resistance=100 package=THT]
  R8 = Resistor [tolerance=±5% resistance=100 package=THT]
  U3 = WS2812 RGB LED strip
  U4 = WS2812 RGB LED strip
  U5 = WS2812 RGB LED strip
  VCC2 = Battery block 9V
  Part5 = Arduino Uno (Rev3)

nets:
  N1: S4.L1, VCC2.+
  GND: S4.COM, R5.Pin_1, C1.-, Part4.GND, U3.GND, U4.GND, U5.GND, VCC2.-, Part5.GND
  N2: S4.L2, R5.Pin_0
  VCC: C1.+, Part4.VCC, U3.VCC, U4.VCC, U5.VCC, Part5.VIN
  N3: Part4.TXD, Part5.D0/RX
  N4: Part4.RXD, Part5.D1/TX
  N5: R6.Pin_0, U5.DIN
  N6: R6.Pin_1, Part5.D4
  N7: R7.Pin_0, U4.DIN
  N8: R7.Pin_1, Part5.D3_PWM
  N9: R8.Pin_0, U3.DIN
  N10: R8.Pin_1, Part5.D2

custom parts:
  WS2812 RGB LED strip: WS2812 strip
